# Fritzing sketch schema (saved by Fritzing 0.9.2b)
breadboards: 1

parts:
  Composant1 = Arduino Uno (Rev3)
  Composant2 = Bluetooth HC-05 Macho

nets:
  N1: Composant1.D9_PWM, Composant2.State
  N2: Composant1.D10_PWM/SS, Composant2.RXD
  N3: Composant1.D11_PWM/MOSI, Composant2.TXD
  5V: Composant1.5V, Composant2.VCC
  GND: Composant1.GND, Composant2.GND
